// Logisim project Contador 0 a 9.circ as structural Verilog
// contador
module _0_a_9 (
  input  q3,
  input  q2,
  input  q1,
  input  q0,
  output d3,
  output d2,
  output d1,
  output d0
);

  wire and_1_out, and_2_out, and_3_out, and_4_out, and_5_out, and_6_out, not_1_out, not_2_out, not_3_out,
       not_4_out, not_5_out;

  and and_1 (and_1_out, q2, q1, q0);
  not not_1 (not_1_out, q2);
  and and_2 (and_2_out, not_1_out, q1, q0);
  and and_3 (and_3_out, q2, not_2_out);
  not not_2 (not_2_out, q1);
  and and_4 (and_4_out, q2, not_3_out);
  not not_3 (not_3_out, q0);
  not not_4 (not_4_out, q1);
  and and_5 (and_5_out, not_4_out, q0);
  and and_6 (and_6_out, q1, not_5_out);
  not not_5 (not_5_out, q0);
  not not_6 (d0, q0);
  or or_1 (d3, and_1_out, q3);
  or or_2 (d2, and_2_out, and_3_out, and_4_out);
  or or_3 (d1, and_5_out, and_6_out);
endmodule

module contador (
  output [3:0] \Saída_do_contador_0_a_9 ,
  output [3:0] \Saída_estado_atual 
);

  wire clock_out, n0_a_9_1_d0, n0_a_9_1_d1, n0_a_9_1_d2, n0_a_9_1_d3, reset_out;

  Clock clock (.out(clock_out));
  Clock #(.highDuration(19), .lowDuration(19)) reset (.out(reset_out));
  D_Flip_Flop d_ff_1 (
    .clk(clock_out), .D(n0_a_9_1_d3), .Q(\Saída_do_contador_0_a_9 [3]), .Qn(\Saída_estado_atual [3]),
    .reset(reset_out));  // open: preset, en
  _0_a_9 u_0_a_9_1 (
    .q3(\Saída_do_contador_0_a_9 [3]), .q2(\Saída_do_contador_0_a_9 [2]), .q1(\Saída_do_contador_0_a_9 [1]),
    .q0(\Saída_do_contador_0_a_9 [0]), .d3(n0_a_9_1_d3), .d2(n0_a_9_1_d2), .d1(n0_a_9_1_d1), .d0(n0_a_9_1_d0));
  D_Flip_Flop d_ff_2 (
    .clk(clock_out), .D(n0_a_9_1_d2), .Q(\Saída_do_contador_0_a_9 [2]), .Qn(\Saída_estado_atual [2]),
    .reset(reset_out));  // open: preset, en
  D_Flip_Flop d_ff_3 (
    .clk(clock_out), .D(n0_a_9_1_d1), .Q(\Saída_do_contador_0_a_9 [1]), .Qn(\Saída_estado_atual [1]),
    .reset(reset_out));  // open: preset, en
  D_Flip_Flop d_ff_4 (
    .clk(clock_out), .D(n0_a_9_1_d0), .Q(\Saída_do_contador_0_a_9 [0]), .Qn(\Saída_estado_atual [0]),
    .reset(reset_out));  // open: preset, en
  Hex_Digit_Display hex_digit_display_1 (.value(\Saída_do_contador_0_a_9 ));  // open: dp
endmodule
